# Fritzing sketch ESP8266-power-10 (saved by Fritzing 0.9.3b)
circuit board: 10cm x 10cm
perfboards: 1

parts:
  U1 = ESP8266 WiFi Module [part_number=ESP8266]
  U2 = ESP8266 WiFi Module [part_number=ESP8266]
  U3 = ESP8266 WiFi Module [part_number=ESP8266]
  U4 = ESP8266 WiFi Module [part_number=ESP8266]
  U5 = ESP8266 WiFi Module [part_number=ESP8266]
  U6 = ESP8266 WiFi Module [part_number=ESP8266]
  U7 = ESP8266 WiFi Module [part_number=ESP8266]
  U8 = ESP8266 WiFi Module [part_number=ESP8266]
  U9 = ESP8266 WiFi Module [part_number=ESP8266]
  U10 = ESP8266 WiFi Module [part_number=ESP8266]
  J1 = male pin header, 1 pin [form="♂ (male)"]
  J4 = male pin header, 1 pin [form="♂ (male)"]
  J5 = male pin header, 1 pin [form="♂ (male)"]
  J2 = male pin header, 1 pin [form="♂ (male)"]
  J6 = screw terminal, 2 pins
  J7 = screw terminal, 2 pins
  J8 = screw terminal, 2 pins

nets:
  VCC: U1.VCC, U1.CH_PD, U2.VCC, U2.CH_PD, U3.VCC, U3.CH_PD, U4.VCC, U4.CH_PD, U5.VCC, U5.CH_PD, U6.VCC, U6.CH_PD, U7.VCC, U7.CH_PD, U8.VCC, U8.CH_PD, U9.VCC, U9.CH_PD, U10.VCC, U10.CH_PD, J1.pin1, J4.pin1, J6.pin1, J7.pin1, J7.pin2
  GND: U1.GND, U2.GND, U3.GND, U4.GND, U5.GND, U6.GND, U7.GND, U8.GND, U9.GND, U10.GND, J5.pin1, J2.pin1, J6.pin2, J8.pin1, J8.pin2

notes:
  Geert de Graaf

custom parts:
  ESP8266 WiFi Module: Generic WiFi Module based on the ESP8266 with onboard PCB antenna and UART communications
